# Fritzing sketch project-sketch-ArduinoUno (saved by Fritzing 0.9.2b)
breadboards: 1

parts:
  U1 = ESP8266 WiFi Module [part_number=ESP8266]
  Part1 = Arduino Uno (Rev3) - ICSP
  kEYPAD_MATRICIAL_1 = KEYPAD 4x3
  SG1 = Buzzer 12mm [package=buzzer-12mm-ns]

nets:
  N1: U1.RXD, Part1.D0/RX
  VCC: U1.VCC, U1.CH_PD, Part1.3V3
  GND: U1.GND, Part1.GND, SG1.1
  N2: U1.TXD, Part1.D1/TX
  N3: Part1.D8, kEYPAD_MATRICIAL_1.arrow1
  N4: Part1.D9_PWM, kEYPAD_MATRICIAL_1.col1
  N5: Part1.D2, SG1.2
  N6: Part1.D3_PWM, kEYPAD_MATRICIAL_1.arrow4
  N7: Part1.D4, kEYPAD_MATRICIAL_1.arrow3
  N8: Part1.D5_PWM, kEYPAD_MATRICIAL_1.col3
  N9: Part1.D6_PWM, kEYPAD_MATRICIAL_1.arrow2
  N10: Part1.D7, kEYPAD_MATRICIAL_1.col2

custom parts:
  ESP8266 WiFi Module: Generic WiFi Module based on the ESP8266 with onboard PCB antenna and UART communications
  KEYPAD 4x3: KEYPAD matricial de 12 botones, 4 filas x 3 columnas
