# Fritzing sketch project-sketch-NodeMcuV3 (saved by Fritzing 0.9.2b)
circuit board: 1.71721cm x 6.85407cm
breadboards: 1

parts:
  Keypad_MATRICIAL_1_3x4 = KEYPAD 4x3
  SG1 = Buzzer 12mm [package=buzzer-12mm-ns]
  U1 = NodeMCU V3.0

nets:
  N1: Keypad_MATRICIAL_1_3x4.col1, U1.D1
  N2: Keypad_MATRICIAL_1_3x4.arrow1, U1.D2
  N3: Keypad_MATRICIAL_1_3x4.col2, U1.D3
  N4: Keypad_MATRICIAL_1_3x4.arrow2, U1.D4
  N5: Keypad_MATRICIAL_1_3x4.col3, U1.D5
  N6: Keypad_MATRICIAL_1_3x4.arrow3, U1.D6
  N7: Keypad_MATRICIAL_1_3x4.arrow4, U1.D7
  N8: SG1.1, U1.D8
  N9: SG1.2, U1.GND

custom parts:
  KEYPAD 4x3: KEYPAD matricial de 12 botones, 4 filas x 3 columnas
  NodeMCU V3.0: ESP8266 based NodeMCU
